# Fritzing sketch anemo (saved by Fritzing 0.9.3b)
breadboards: 1

parts:
  J1 = screw terminal, 3 pins
  HLK-PM1 = HLK-PM01
  Part1 = Adafruit ADS1115 16Bit I2C ADC [part_number="Adafruit #1085"]
  Raspberry_Pi_Zero1 = Raspberry Pi Zero
  J2 = female pin header, 2 pins [form="♀ (female)" part_number="wind vane"]
  R1 = Resistor [tolerance=±5% resistance=10k package=THT]
  J3 = female pin header, 2 pins [form="♀ (female)" part_number=rain]
  J4 = female pin header, 3 pins [form="♀ (female)"]
  J5 = female pin header, 2 pins [form="♀ (female)" part_number=anemo]
  LED1 = smd LED [color="Red (633nm)" package="1206 [SMD]"]
  R2 = Resistor [tolerance=±5% resistance=330 package="1206 [SMD]"]

nets:
  N1: J1.pin1, HLK-PM1.AC#0
  N2: J1.pin3, HLK-PM1.AC#1
  N3: HLK-PM1.-Vo, Part1.GND, J2.pin2, J4.pin1, R2.Pin_0
  VDD: HLK-PM1.+Vo, Part1.VDD, Raspberry_Pi_Zero1.5V, R1.Pin_0, J3.pin2, J4.pin2, J5.pin2
  N4: Part1.AIN1, J4.pin3
  N5: Part1.AIN0, J2.pin1, R1.Pin_1
  N6: Part1.SDA, Raspberry_Pi_Zero1.GPIO2
  N7: Part1.SCL, Raspberry_Pi_Zero1.GPIO3
  N8: Raspberry_Pi_Zero1.GPIO24, J3.pin1
  N9: Raspberry_Pi_Zero1.GPIO23, J5.pin1
  N10: Raspberry_Pi_Zero1.GPIO18, LED1.anode
  N11: LED1.cathode, R2.Pin_1

custom parts:
  Adafruit ADS1115 16Bit I2C ADC: For microcontrollers without an analog-to-digital converter or when you want a higher-precision ADC, the ADS1115 provides 16-bit precision at 860 samples/second over I2C. The chip can be configured as 4 single-ended input channels, or two differential channels. As a nice bonus, it even includes a programmable gain amplifier, up to x16, to help boost up smaller single/differential signals to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
